// Logisim project Lab1_PartA_Circuit.circ as structural Verilog: 1 circuit, main circuit main
module main (
  input  A,
  input  B,
  input  C,
  output S,
  output O
);

  wire AND1_out, AND2_out, XOR1_out;

  xor XOR1 (XOR1_out, A, B);
  and AND1 (AND1_out, A, B);
  xor XOR2 (S, XOR1_out, C);
  and AND2 (AND2_out, XOR1_out, C);
  or OR1 (O, AND2_out, AND1_out);
endmodule
