// Logisim project Lab1_PartB_Circuit.circ as structural Verilog: 2 circuits, main circuit main
module main (
  input  d1,
  input  d2,
  input  d3
);

  wire namelogic_1_1_d5, namelogic_1_1_s0, namelogic_1_1_s1, namelogic_1_1_s2, namelogic_1_1_s3,
       namelogic_1_1_s4, namelogic_1_1_s6;

  namelogic_1 namelogic_1_1 (
    .d1(d1), .d2(d2), .d3(d3), .d5(namelogic_1_1_d5), .s0(namelogic_1_1_s0), .s4(namelogic_1_1_s4),
    .s1(namelogic_1_1_s1), .s2(namelogic_1_1_s2), .s6(namelogic_1_1_s6), .s3(namelogic_1_1_s3));
  _7_Segment_Display u_7_segment_display_1 (
    .g(namelogic_1_1_s6), .f(namelogic_1_1_d5), .a(namelogic_1_1_s0), .b(namelogic_1_1_s1),
    .e(namelogic_1_1_s4), .d(namelogic_1_1_s3), .c(namelogic_1_1_s2));  // open: dp
endmodule

module namelogic_1 (
  input  d1,
  input  d2,
  input  d3,
  output d5,
  output s0,
  output s4,
  output s1,
  output s2,
  output s6,
  output s3
);

  wire and_1_out, and_2_out, and_3_out, and_4_out, and_5_out, and_7_out, and_8_out, and_9_out, and_11_out,
       not_2_out, not_3_out;

  or or_1 (s4, and_1_out, and_2_out, and_3_out);
  or or_2 (s6, and_4_out, and_5_out);
  and and_1 (and_1_out, d1, not_2_out, not_3_out);
  and and_2 (and_2_out, d5, d3);
  and and_3 (and_3_out, d5, d2);
  and and_4 (and_4_out, not_2_out, not_3_out);
  and and_5 (and_5_out, d2, d5);
  not not_1 (d5, d1);
  not not_2 (not_2_out, d2);
  not not_3 (not_3_out, d3);
  and and_6 (s0, d5, d2);
  and and_7 (and_7_out, d5, not_2_out, not_3_out);
  and and_8 (and_8_out, not_2_out, not_3_out);
  and and_9 (and_9_out, d5, d2, d3);
  and and_10 (s3, d5, not_2_out, not_3_out);
  or or_3 (s2, and_8_out, and_9_out);
  and and_11 (and_11_out, d5, d2, d3);
  or or_4 (s1, and_7_out, and_11_out);
endmodule
