// Logisim project lab3a.circ as structural Verilog: 1 circuit, main circuit mux2to1
module mux2to1 (
  input  [3:0] X,
  input  S,
  input  [3:0] Y,
  output [3:0] M
);

  wire [3:0] and_1_out, and_2_out, not_1_out;

  assign not_1_out = ~{4{S}};  // NOT_Gate not_1, 4 bits wide
  assign and_1_out = X & not_1_out;  // AND_Gate and_1, 4 bits wide
  assign and_2_out = {4{S}} & Y;  // AND_Gate and_2, 4 bits wide
  assign M = and_1_out | and_2_out;  // OR_Gate or_1, 4 bits wide
endmodule
