// Logisim project lab3b.circ as structural Verilog: 2 circuits, main circuit fa
module fa (
  input  X,
  input  Y,
  input  Cin,
  output S,
  output Cout
);

  wire and_1_out, and_2_out, xor_1_out;

  and and_1 (and_1_out, X, Y);
  and and_2 (and_2_out, xor_1_out, Cin);
  or or_1 (Cout, and_1_out, and_2_out);
  xor xor_1 (xor_1_out, X, Y);
  xor xor_2 (S, xor_1_out, Cin);
endmodule

module adder4 (
  input  Sub,
  input  [3:0] X,
  input  [3:0] Y,
  output C,
  output [3:0] S
);

  wire fa_2_cout, fa_3_cout, fa_4_cout, xor_1_out, xor_2_out, xor_3_out, xor_4_out;

  xor xor_1 (xor_1_out, Y[3], Sub);
  fa fa_1 (.X(X[3]), .Y(xor_1_out), .Cin(fa_2_cout), .S(S[3]), .Cout(C));
  xor xor_2 (xor_2_out, Y[2], Sub);
  fa fa_2 (.X(X[2]), .Y(xor_2_out), .Cin(fa_3_cout), .S(S[2]), .Cout(fa_2_cout));
  xor xor_3 (xor_3_out, Y[1], Sub);
  fa fa_3 (.X(X[1]), .Y(xor_3_out), .Cin(fa_4_cout), .S(S[1]), .Cout(fa_3_cout));
  xor xor_4 (xor_4_out, Y[0], Sub);
  fa fa_4 (.X(X[0]), .Y(xor_4_out), .Cin(Sub), .S(S[0]), .Cout(fa_4_cout));
endmodule
