// Logisim project lab3c.circ as structural Verilog: 2 circuits, main circuit main
module ALU (
  input  [1:0] func,
  input  [3:0] X,
  input  [3:0] Y,
  output [3:0] Z
);

  wire [3:0] adder4_1_s, and_1_out, mux2to1_1_m, or_1_out;

  assign and_1_out = X & Y;  // AND_Gate and_1, 4 bits wide
  assign or_1_out = X | Y;  // OR_Gate or_1, 4 bits wide
  adder4 adder4_1 (.Sub(func[0]), .X(X), .Y(Y), .S(adder4_1_s));  // open: C
  mux2to1 mux2to1_1 (.X(and_1_out), .S(func[0]), .Y(or_1_out), .M(mux2to1_1_m));
  Hex_Digit_Display hex_digit_display_1 (.value(Z));  // open: dp
  mux2to1 mux2to1_2 (.X(adder4_1_s), .S(func[1]), .Y(mux2to1_1_m), .M(Z));
endmodule

module main (
  output [3:0] Z
);

  wire [1:0] func_sw2;
  wire [3:0] X_sw4, Y_sw4;

  DipSwitch #(.number(2)) func (.sw1(func_sw2[1]), .sw2(func_sw2[0]));
  DipSwitch #(.number(4)) X (.sw1(X_sw4[3]), .sw2(X_sw4[2]), .sw3(X_sw4[1]), .sw4(X_sw4[0]));
  DipSwitch #(.number(4)) Y (.sw1(Y_sw4[3]), .sw2(Y_sw4[2]), .sw3(Y_sw4[1]), .sw4(Y_sw4[0]));
  LED led_1 (.in(func_sw2[1]));
  LED led_2 (.in(func_sw2[0]));
  Hex_Digit_Display hex_digit_display_1 (.value(X_sw4));  // open: dp
  Hex_Digit_Display hex_digit_display_2 (.value(Y_sw4));  // open: dp
  Hex_Digit_Display hex_digit_display_3 (.value(Z));  // open: dp
  ALU alu_1 (.func(func_sw2), .X(X_sw4), .Y(Y_sw4), .Z(Z));
endmodule
