// Logisim project Lab2_PartB_Circuit.circ as structural Verilog: 3 circuits, main circuit SRlatch
module SRlatch (
  input  S,
  input  Clock,
  input  R,
  output notQ,
  output Q
);

  wire and_1_out, and_2_out;

  and and_1 (and_1_out, S, Clock);
  and and_2 (and_2_out, Clock, R);
  nor nor_1 (notQ, and_1_out, Q);
  nor nor_2 (Q, notQ, and_2_out);
endmodule

module Dlatch (
  input  D,
  input  C,
  output notQ,
  output Q
);

  wire not_1_out;

  not not_1 (not_1_out, D);
  SRlatch srlatch_1 (.S(D), .Clock(C), .R(not_1_out), .notQ(notQ), .Q(Q));
endmodule

module PDfilpflop (
  input  D,
  input  C,
  output notQ,
  output Q
);

  wire dlatch_1_q, not_1_out, not_2_out;

  not not_1 (not_1_out, C);
  not not_2 (not_2_out, not_1_out);
  Dlatch dlatch_1 (.D(D), .C(not_1_out), .Q(dlatch_1_q));  // open: notQ
  Dlatch dlatch_2 (.D(dlatch_1_q), .C(not_2_out), .notQ(notQ), .Q(Q));
endmodule
