// Logisim project Lab3_PartA_gate_control_system.circ as structural Verilog: 3 circuits, main circuit main
module main (
);

  wire AB_sw1, AB_sw2, Clk_out, d_ff_1_q, d_ff_2_q, outputlogic_1_l, outputlogic_1_r, reset_out,
       statelogic_1_newf1, statelogic_1_newf2;

  Button Clk (.out(Clk_out));
  Button reset (.out(reset_out));
  DipSwitch #(.number(2)) AB (.sw1(AB_sw1), .sw2(AB_sw2));
  statelogic statelogic_1 (
    .A(AB_sw1), .B(AB_sw2), .F2(d_ff_1_q), .F1(d_ff_2_q), .newF2(statelogic_1_newf2),
    .newF1(statelogic_1_newf1));
  D_Flip_Flop d_ff_1 (.D(statelogic_1_newf2), .clk(Clk_out), .Q(d_ff_1_q), .reset(reset_out));  // open: Qn, preset
  D_Flip_Flop d_ff_2 (.D(statelogic_1_newf1), .clk(Clk_out), .Q(d_ff_2_q), .reset(reset_out));  // open: Qn, preset
  LED L (.in(outputlogic_1_l));
  outputlogic outputlogic_1 (.F2(d_ff_1_q), .F1(d_ff_2_q), .L(outputlogic_1_l), .R(outputlogic_1_r));
  LED R (.in(outputlogic_1_r));
endmodule

module statelogic (
  input  A,
  input  B,
  input  F2,
  input  F1,
  output newF2,
  output newF1
);

  wire and_1_out, and_2_out, and_3_out, and_4_out, and_5_out, and_6_out, and_7_out, not_1_out, not_2_out,
       not_3_out, not_4_out;

  not not_1 (not_1_out, A);
  not not_2 (not_2_out, B);
  not not_3 (not_3_out, F2);
  not not_4 (not_4_out, F1);
  and and_1 (and_1_out, not_1_out, not_2_out);
  and and_2 (and_2_out, not_3_out, F1, B);
  and and_3 (and_3_out, F2, not_4_out, B);
  and and_4 (and_4_out, not_1_out, not_3_out, F1);
  and and_5 (and_5_out, not_1_out, F2, not_4_out);
  and and_6 (and_6_out, A, not_3_out, not_4_out);
  and and_7 (and_7_out, A, F2, F1);
  or or_1 (newF2, and_1_out, and_2_out, and_3_out);
  or or_2 (newF1, and_4_out, and_5_out, and_6_out, and_7_out, not_2_out);
endmodule

module outputlogic (
  input  F2,
  input  F1,
  output L,
  output R
);

  wire not_1_out;

  not not_1 (not_1_out, F2);
  and and_1 (L, F2, F1);
  and and_2 (R, not_1_out, F1);
endmodule
