// Logisim project lab04_base.circ as structural Verilog: 4 circuits, main circuit main
module register_file (
  input  [7:0] data_write,
  input  write_enable,
  input  [1:0] write_reg,
  input  clk,
  input  [1:0] read_reg,
  input  reset,
  input  clear,
  output [7:0] data_read
);

  wire and_1_out, and_2_out, and_3_out, and_4_out;
  wire [3:0] multiplexer_1_out;
  wire [7:0] and_5_out, and_6_out, and_7_out, and_8_out, R0_q, R1_q, R2_q, R3_q;
  wire [7:7] not_1_out;

  not not_1 (not_1_out[7], clear);
  Multiplexer #(.select(2), .width(4)) multiplexer_1 (
    .in0(4'b0001), .in1(4'b0010), .in2(4'b0100), .in3(4'b1000), .out(multiplexer_1_out), .sel(write_reg));
  and and_1 (and_1_out, write_enable, multiplexer_1_out[0]);
  and and_2 (and_2_out, write_enable, multiplexer_1_out[1]);
  and and_3 (and_3_out, write_enable, multiplexer_1_out[2]);
  and and_4 (and_4_out, write_enable, multiplexer_1_out[3]);
  Register R0 (.D(and_5_out), .en(and_1_out), .clk(clk), .Q(R0_q), .clr(reset));
  assign and_5_out = data_write & {8{not_1_out[7]}};  // AND_Gate and_5, 8 bits wide
  Register R1 (.D(and_6_out), .en(and_2_out), .clk(clk), .Q(R1_q), .clr(reset));
  assign and_6_out = data_write & {8{not_1_out[7]}};  // AND_Gate and_6, 8 bits wide
  Register R2 (.D(and_7_out), .en(and_3_out), .clk(clk), .Q(R2_q), .clr(reset));
  assign and_7_out = data_write & {8{not_1_out[7]}};  // AND_Gate and_7, 8 bits wide
  Register R3 (.D(and_8_out), .en(and_4_out), .clk(clk), .Q(R3_q), .clr(reset));
  assign and_8_out = data_write & {8{not_1_out[7]}};  // AND_Gate and_8, 8 bits wide
  Multiplexer #(.select(2), .width(8)) multiplexer_2 (
    .in0(R0_q), .in1(R1_q), .in2(R2_q), .in3(R3_q), .out(data_read), .sel(read_reg));
endmodule

module alu (
  input  [7:0] A,
  input  [7:0] B,
  input  op,
  output [7:0] data_out
);

  wire [7:0] adder_1_out, multiplier_1_out;

  Adder adder_1 (.a(A), .b(B), .out(adder_1_out));  // open: cin, cout
  Multiplier multiplier_1 (.a(A), .b(B), .out(multiplier_1_out));  // open: cin, cout
  Multiplexer #(.width(8)) multiplexer_1 (.in0(adder_1_out), .in1(multiplier_1_out), .out(data_out), .sel(op));
endmodule

module instr_decoder (
  input  [7:0] instr,
  output [1:0] imm,
  output [1:0] read_reg,
  output [1:0] write_reg,
  output write_en,
  output alu_op,
  output reg_clear
);

  or or_1 (write_en, instr[6], instr[7]);
  and and_1 (reg_clear, instr[6], instr[7]);

  assign alu_op = instr[7];
  assign imm = instr[1:0];
  assign read_reg = instr[3:2];
  assign write_reg = instr[5:4];
endmodule

module main (
  input  [7:0] instr
);

  wire CLK_out, instr_decoder_1_alu_op, instr_decoder_1_reg_clear, instr_decoder_1_write_en, reset_out;
  wire [1:0] instr_decoder_1_imm, instr_decoder_1_read_reg, instr_decoder_1_write_reg;
  wire [7:0] alu_1_data_out, bit_extender_1_out, register_file_1_data_read;

  Button CLK (.out(CLK_out));
  Button reset (.out(reset_out));
  instr_decoder instr_decoder_1 (
    .instr(instr), .imm(instr_decoder_1_imm), .read_reg(instr_decoder_1_read_reg),
    .write_reg(instr_decoder_1_write_reg), .write_en(instr_decoder_1_write_en),
    .alu_op(instr_decoder_1_alu_op), .reg_clear(instr_decoder_1_reg_clear));
  assign bit_extender_1_out = {{6{1'b0}}, instr_decoder_1_imm};  // Bit_Extender bit_extender_1
  register_file register_file_1 (
    .data_write(alu_1_data_out), .write_enable(instr_decoder_1_write_en),
    .write_reg(instr_decoder_1_write_reg), .clk(CLK_out), .read_reg(instr_decoder_1_read_reg),
    .reset(reset_out), .clear(instr_decoder_1_reg_clear), .data_read(register_file_1_data_read));
  alu alu_1 (
    .A(register_file_1_data_read), .B(bit_extender_1_out), .op(instr_decoder_1_alu_op),
    .data_out(alu_1_data_out));
endmodule
